# Fritzing sketch ReedSample_pulup (saved by Fritzing 0.9.3b)
breadboards: 1

parts:
  Raspberry_Pi_1 = Raspberry Pi 4 [part_number=RPI-4-b]
  R1 = Resistor [tolerance=±5% resistance=1k package=THT]
  R2 = Resistor [tolerance=±5% resistance=330 package=THT]
  LED1 = LED - 5mm [color="Red (633nm)" package="5 mm [THT]"]
  S1 = TILT-SWITCH-SW-200D [package=reed_switch_plastic]

nets:
  N1: Raspberry_Pi_1.GPIO2, LED1.cathode
  N2: Raspberry_Pi_1.GND, R1.Pin_1, R2.Pin_0
  N3: Raspberry_Pi_1.GPIO14, R1.Pin_0, S1.1
  N4: Raspberry_Pi_1.5V, S1.2
  N5: R2.Pin_1, LED1.anode

custom parts:
  Raspberry Pi 4: The RPi4, a faster version of the awesome Raspberry Pi 2 B ARM Board with 40 pin gpio. Ready for special Raspberry Pi B+ and RPi2 Hat (Hardware attached (on) top)
